# Fritzing sketch Arduino-Cottage-Monitoring-System (saved by Fritzing 0.9.1b)
breadboards: 1

parts:
  U5 = mystery part, 3 pins [chip_label=DS18B20 spacing=300mil]
  R1 = Resistor [tolerance=±5% resistance=4.7k package=THT]
  VCC1 = Battery block 9V
  D1 = Rectifier Diode [part_number=1N4001 package="300 mil [THT]"]
  U6 = Optocoupler [package=THT]
  J1 = Power Jack [package=power_jack_pth_lock]
  R2 = Resistor [tolerance=±5% resistance=680 package=THT]
  R3 = Resistor [tolerance=±5% resistance=12k package=THT]
  R4 = Resistor [tolerance=±5% resistance=1M package=THT]
  R5 = Resistor [tolerance=±5% resistance=1M package=THT]
  part = Rectifier Diode [part_number=1N4001 package="300 mil [THT]"]  # not connected
  Arduino1 = Arduino Uno (Rev3)
  U7 = RF-LINK_RX [package=rf-link_rx]
  ANT1 = Antenna
  JP1 = RCA [package=rca_lock]

nets:
  GND: U5.pin1, U5.pin3, VCC1.-, U6.Pin_4, R5.Pin_1, Arduino1.GND, U7.GND, JP1.SHELL
  N1: U5.pin2, R1.Pin_0, Arduino1.D2
  5V: R1.Pin_1, R3.Pin_0, Arduino1.5V, U7.+5V
  N2: VCC1.+, D1.anode, R4.Pin_0
  N3: D1.cathode, Arduino1.VIN
  N4: U6.Pin_1, R2.Pin_1
  N5: U6.Pin_2, J1.GND, J1.GNDBREAK
  N6: U6.Pin_5, R3.Pin_1, Arduino1.D8
  N7: J1.PWR, R2.Pin_0
  N8: R4.Pin_1, R5.Pin_0, Arduino1.A2
  N9: Arduino1.D5_PWM, JP1.PIN
  N10: Arduino1.D7, U7.DATA
  N11: U7.ANT, ANT1.antenna_lead
