# Fritzing sketch Arduino-Cottage-Monitoring-System_Siren-switch-box (saved by Fritzing 0.9.1b)
breadboards: 1

parts:
  Q1 = npn-Powertransistor [part_number=BU406 package="TO220 [THT]"]
  R4 = Resistor [tolerance=±5% resistance=390 package=THT]
  JP1 = RCA [part_number=RCA package=rca_lock]
  J1 = Power Jack [part_number="DC Jack " package=power_jack_slot]
  J2 = Piezo Speaker [part_number=Siren]

nets:
  N1: Q1.base, R4.Pin_1
  N2: Q1.collector, J2.pin1
  N3: Q1.emitter, JP1.SHELL, J1.GND
  N4: R4.Pin_0, JP1.SWITCH
  N5: J1.PWR, J2.pin2
